# Fritzing sketch schematics (saved by Fritzing 0.9.1b)
breadboards: 1

parts:
  T1 = LM35 Temperature Sensor [package="TO92 [THT]"]
  LCD1 = LCD screen
  RE1 = Rotary Encoder [package=THT]
  S1 = Pushbutton [package="[THT]"]
  S2 = Pushbutton [package="[THT]"]
  S3 = Pushbutton [package="[THT]"]
  Componente2 = Arduino Mega 2560 (Rev3)
  R1 = Resistor [tolerance=±5% resistance=10k package=THT]
  R3 = Resistor [tolerance=±5% resistance=10k package=THT]
  LED1 = LED - 5mm [color="Red (633nm)" package="5 mm [THT]"]
  R4 = Resistor [tolerance=±5% resistance=300 package=THT]
  LED2 = LED - 5mm [color="Green (555nm)" package="5 mm [THT]"]
  Componente3 = Arduino Ethernet Shield (Rev3)
  R5 = Resistor [tolerance=±5% resistance=300 package=THT]
  R2 = Resistor [tolerance=±5% resistance=10k package=THT]

nets:
  VDD: T1.+Vs, LCD1.VDD, LCD1.LED+, RE1.EncoderPinB, S1.Pin_3, S1.Pin_4, S2.Pin_3, S2.Pin_4, S3.Pin_3, S3.Pin_4, Componente3.5V
  N1: T1.Vout, Componente2.A0
  GND: T1.GND, LCD1.VSS, LCD1.R/W, LCD1.LED-, RE1.EncoderPinA, R1.Pin_1, R3.Pin_1, LED1.cathode, LED2.cathode, Componente3.GND
  N2: LCD1.V0, RE1.EncoderPinC
  N3: LCD1.RS, Componente2.D33
  N4: LCD1.E, Componente2.D35
  N5: LCD1.DB4, Componente2.D37
  N6: LCD1.DB5, Componente2.D39
  N7: LCD1.DB6, Componente2.D41
  N8: LCD1.DB7, Componente2.D43
  N9: S1.Pin_1, S1.Pin_2, Componente2.D22, R1.Pin_0
  N10: S2.Pin_1, S2.Pin_2, Componente2.D24, R2.Pin_0
  N11: S3.Pin_1, S3.Pin_2, Componente2.D26, R3.Pin_0
  N12: Componente2.D46, R5.Pin_0
  N13: Componente2.D48, R4.Pin_1
  N14: LED1.anode, R5.Pin_1
  N15: R4.Pin_0, LED2.anode
